// Logisim project FullAdder.circ as structural Verilog
module FullAdder (
  input  A,
  input  B,
  input  Carry_In,
  output Sum,
  output Carry_Out
);

  wire and_1_out, and_2_out, and_3_out, or_1_out, xor_1_out;

  xor xor_1 (xor_1_out, A, B);
  and and_1 (and_1_out, A, B);
  and and_2 (and_2_out, A, Carry_In);
  and and_3 (and_3_out, B, Carry_In);
  xor xor_2 (Sum, xor_1_out, Carry_In);
  or or_1 (or_1_out, and_1_out, and_2_out);
  or or_2 (Carry_Out, or_1_out, and_3_out);
endmodule
