// Logisim project 3bit_4way_selector.circ as structural Verilog: 2 circuits, main circuit main
module main (
  input  S_1,
  input  S_0,
  input  InA_0,
  input  InA_1,
  input  InA_2,
  input  InB_0,
  input  InB_1,
  input  InB_2,
  input  InC_0,
  input  InC_1,
  input  InC_2,
  input  InD_0,
  input  InD_1,
  input  InD_2,
  output Result_0,
  output Result_1,
  output Result2
);

  selector_1bit_4way selector_1bit_4way_1 (
    .S_1(S_1), .S_0(S_0), .InA(InA_0), .InB(InB_0), .InC(InC_0), .InD(InD_0), .Result(Result_0));
  selector_1bit_4way selector_1bit_4way_2 (
    .S_1(S_1), .S_0(S_0), .InA(InA_1), .InB(InB_1), .InC(InC_1), .InD(InD_1), .Result(Result_1));
  selector_1bit_4way selector_1bit_4way_3 (
    .S_1(S_1), .S_0(S_0), .InA(InA_2), .InB(InB_2), .InC(InC_2), .InD(InD_2), .Result(Result2));
endmodule

module selector_1bit_4way (
  input  S_1,
  input  S_0,
  input  InA,
  input  InB,
  input  InC,
  input  InD,
  output Result
);

  wire and_1_out, and_2_out, and_3_out, and_4_out, and_5_out, and_6_out, and_7_out, and_8_out, not_1_out,
       not_2_out, or_1_out, or_3_out;

  not not_1 (not_1_out, S_1);
  not not_2 (not_2_out, S_0);
  and and_1 (and_1_out, not_1_out, not_2_out);
  and and_2 (and_2_out, not_1_out, S_0);
  and and_3 (and_3_out, S_1, not_2_out);
  and and_4 (and_4_out, S_1, S_0);
  and and_5 (and_5_out, and_1_out, InA);
  and and_6 (and_6_out, and_2_out, InB);
  and and_7 (and_7_out, and_3_out, InC);
  and and_8 (and_8_out, and_4_out, InD);
  or or_1 (or_1_out, and_5_out, and_6_out);
  or or_2 (Result, or_1_out, or_3_out);
  or or_3 (or_3_out, and_7_out, and_8_out);

  // Notes on the sheet:
  //   !S_0
  //   !S_1
endmodule
