// Logisim project 4bit_Comparator.circ as structural Verilog: 2 circuits, main circuit main
module main (
  input  in_1,
  input  in_2,
  input  in_3,
  input  in_4,
  input  in_5,
  input  in_6,
  input  in_7,
  input  in_8
);

  wire comparator_4bit_1_equal;

  Comparator_4bit comparator_4bit_1 (
    .A_0(in_1), .B_0(in_2), .A_1(in_3), .B_1(in_4), .A_2(in_5), .B_2(in_6), .A_3(in_7), .B_3(in_8),
    .Equal(comparator_4bit_1_equal));
  LED led_1 (.in(comparator_4bit_1_equal));
endmodule

module Comparator_4bit (
  input  A_0,
  input  B_0,
  input  A_1,
  input  B_1,
  input  A_2,
  input  B_2,
  input  A_3,
  input  B_3,
  output Equal
);

  wire and_1_out, and_2_out, not_1_out, not_2_out, not_3_out, not_4_out, xor_1_out, xor_2_out, xor_3_out,
       xor_4_out;

  xor xor_1 (xor_1_out, A_0, B_0);
  xor xor_2 (xor_2_out, A_1, B_1);
  xor xor_3 (xor_3_out, A_2, B_2);
  xor xor_4 (xor_4_out, A_3, B_3);
  not not_1 (not_1_out, xor_1_out);
  not not_2 (not_2_out, xor_2_out);
  not not_3 (not_3_out, xor_3_out);
  not not_4 (not_4_out, xor_4_out);
  and and_1 (and_1_out, not_1_out, not_2_out);
  and and_2 (and_2_out, not_3_out, not_4_out);
  and and_3 (Equal, and_1_out, and_2_out);
endmodule
