// Logisim project QZX_Adder.circ as structural Verilog: 4 circuits, main circuit main
module main (
  input  [3:0] A,
  input  [3:0] B
);

  wire adder_4bit_1_carry_out;
  wire [3:0] adder_4bit_1_sum;

  Hex_Digit_Display hex_digit_display_1 (.value(A));  // open: dp
  Hex_Digit_Display hex_digit_display_2 (.value(B));  // open: dp
  LED Carry (.in(adder_4bit_1_carry_out));
  adder_4bit adder_4bit_1 (.A(A), .B(B), .carry_out(adder_4bit_1_carry_out), .sum(adder_4bit_1_sum));  // open: carry_in
  Hex_Digit_Display hex_digit_display_3 (.value(adder_4bit_1_sum));  // open: dp
endmodule

module half_adder (
  input  bit_0,
  input  bit_1,
  output carry,
  output sum
);

  and and_1 (carry, bit_0, bit_1);
  xor xor_1 (sum, bit_0, bit_1);
endmodule

module full_adder (
  input  carry_in,
  input  bit_1,
  input  bit_0,
  output carry_out,
  output sum
);

  wire half_adder_1_carry, half_adder_1_sum, half_adder_2_carry;

  half_adder half_adder_1 (.bit_0(carry_in), .bit_1(bit_1), .carry(half_adder_1_carry), .sum(half_adder_1_sum));
  or or_1 (carry_out, half_adder_1_carry, half_adder_2_carry);
  half_adder half_adder_2 (.bit_0(half_adder_1_sum), .bit_1(bit_0), .carry(half_adder_2_carry), .sum(sum));
endmodule

module adder_4bit (
  input  [3:0] A,
  input  [3:0] B,
  input  carry_in,
  output carry_out,
  output [3:0] sum
);

  wire full_adder_2_carry_out, full_adder_3_carry_out, full_adder_4_carry_out;

  full_adder full_adder_1 (
    .carry_in(full_adder_2_carry_out), .bit_1(A[3]), .bit_0(B[3]), .carry_out(carry_out), .sum(sum[3]));
  full_adder full_adder_2 (
    .carry_in(full_adder_3_carry_out), .bit_1(A[2]), .bit_0(B[2]), .carry_out(full_adder_2_carry_out),
    .sum(sum[2]));
  full_adder full_adder_3 (
    .carry_in(full_adder_4_carry_out), .bit_1(A[1]), .bit_0(B[1]), .carry_out(full_adder_3_carry_out),
    .sum(sum[1]));
  full_adder full_adder_4 (
    .carry_in(carry_in), .bit_1(A[0]), .bit_0(B[0]), .carry_out(full_adder_4_carry_out), .sum(sum[0]));
endmodule
