// Logisim project SignedAdder.circ as structural Verilog
module Full_Subtracter (
  input  bit_1,
  input  bit_0,
  input  borrow_in,
  output borrow_out,
  output diff
);

  wire half_subtracter_1_borrow, half_subtracter_1_diff, half_subtracter_2_borrow;

  Half_Subtracter half_subtracter_1 (
    .bit_1(bit_1), .bit_0(bit_0), .borrow(half_subtracter_1_borrow), .diff(half_subtracter_1_diff));
  Half_Subtracter half_subtracter_2 (
    .bit_1(half_subtracter_1_diff), .bit_0(borrow_in), .borrow(half_subtracter_2_borrow), .diff(diff));
  or or_1 (borrow_out, half_subtracter_1_borrow, half_subtracter_2_borrow);
endmodule

module Half_Subtracter (
  input  bit_1,
  input  bit_0,
  output borrow,
  output diff
);

  wire not_1_out;

  not not_1 (not_1_out, bit_1);
  and and_1 (borrow, not_1_out, bit_0);
  xor xor_1 (diff, bit_1, bit_0);
endmodule

module Subtracter_4bit (
  input  borrow_in,
  input  [3:0] A,
  input  [3:0] B,
  output [3:0] diff,
  output borrow_out
);

  wire full_subtracter_1_borrow_out, full_subtracter_2_borrow_out, full_subtracter_3_borrow_out;

  Full_Subtracter full_subtracter_1 (
    .bit_1(A[0]), .bit_0(B[0]), .borrow_in(borrow_in), .borrow_out(full_subtracter_1_borrow_out),
    .diff(diff[0]));
  Full_Subtracter full_subtracter_2 (
    .bit_1(A[1]), .bit_0(B[1]), .borrow_in(full_subtracter_1_borrow_out),
    .borrow_out(full_subtracter_2_borrow_out), .diff(diff[1]));
  Full_Subtracter full_subtracter_3 (
    .bit_1(A[2]), .bit_0(B[2]), .borrow_in(full_subtracter_2_borrow_out),
    .borrow_out(full_subtracter_3_borrow_out), .diff(diff[2]));
  Full_Subtracter full_subtracter_4 (
    .bit_1(A[3]), .bit_0(B[3]), .borrow_in(full_subtracter_3_borrow_out), .borrow_out(borrow_out),
    .diff(diff[3]));

  // Other names for the same wires on the sheet: A_0 = A[0]; A_1 = A[1]; A_2 = A[2]; A_3 = A[3]; B_0 = B[0];
  //   B_1 = B[1]; B_2 = B[2]; B_3 = B[3]
endmodule

module half_adder (
  input  bit_0,
  input  bit_1,
  output carry,
  output sum
);

  and and_1 (carry, bit_0, bit_1);
  xor xor_1 (sum, bit_0, bit_1);
endmodule

module full_adder (
  input  carry_in,
  input  bit_1,
  input  bit_0,
  output carry_out,
  output sum
);

  wire half_adder_1_carry, half_adder_1_sum, half_adder_2_carry;

  half_adder half_adder_1 (.bit_0(carry_in), .bit_1(bit_1), .carry(half_adder_1_carry), .sum(half_adder_1_sum));
  or or_1 (carry_out, half_adder_1_carry, half_adder_2_carry);
  half_adder half_adder_2 (.bit_0(half_adder_1_sum), .bit_1(bit_0), .carry(half_adder_2_carry), .sum(sum));
endmodule

module adder_4bit (
  input  [3:0] A,
  input  [3:0] B,
  input  carry_in,
  output carry_out,
  output [3:0] sum
);

  wire full_adder_2_carry_out, full_adder_3_carry_out, full_adder_4_carry_out;

  full_adder full_adder_1 (
    .carry_in(full_adder_2_carry_out), .bit_1(A[3]), .bit_0(B[3]), .carry_out(carry_out), .sum(sum[3]));
  full_adder full_adder_2 (
    .carry_in(full_adder_3_carry_out), .bit_1(A[2]), .bit_0(B[2]), .carry_out(full_adder_2_carry_out),
    .sum(sum[2]));
  full_adder full_adder_3 (
    .carry_in(full_adder_4_carry_out), .bit_1(A[1]), .bit_0(B[1]), .carry_out(full_adder_3_carry_out),
    .sum(sum[1]));
  full_adder full_adder_4 (
    .carry_in(carry_in), .bit_1(A[0]), .bit_0(B[0]), .carry_out(full_adder_4_carry_out), .sum(sum[0]));
endmodule

module TureForm_Adder_4bit (
  input  [3:0] A,
  input  [3:0] B,
  output [3:0] Result
);

  wire A_GreaterThan_B, IsSameSign, not_2_out, not_3_out, not_4_out, not_5_out, subtracter_4bit_1_borrow_out,
       subtracter_4bit_2_borrow_out, xor_1_out;
  wire [3:0] A_Minus_B, A_Plus_B, B_Minus_A, Minus_Ans;
  wire [3:3] multiplexer_1_out;

  xor xor_1 (xor_1_out, A[3], B[3]);
  not not_1 (IsSameSign, xor_1_out);
  Subtracter_4bit subtracter_4bit_1 (
    .A({1'b0, A[2:0]}), .B({1'b0, B[2:0]}), .diff(A_Minus_B), .borrow_out(subtracter_4bit_1_borrow_out));  // open: borrow_in
  Subtracter_4bit subtracter_4bit_2 (
    .A({1'b0, B[2:0]}), .B({1'b0, A[2:0]}), .diff(B_Minus_A), .borrow_out(subtracter_4bit_2_borrow_out));  // open: borrow_in
  adder_4bit adder_4bit_1 (.A({1'b0, A[2:0]}), .B({1'b0, B[2:0]}), .sum(A_Plus_B));  // open: carry_in, carry_out
  not not_2 (not_2_out, subtracter_4bit_1_borrow_out);
  and and_1 (A_GreaterThan_B, not_2_out, subtracter_4bit_2_borrow_out);
  Multiplexer #(.width(4)) multiplexer_1 (
    .in0(A_Minus_B), .in1(B_Minus_A), .out({multiplexer_1_out[3], Minus_Ans[2:0]}), .sel(not_3_out));
  not not_3 (not_3_out, A_GreaterThan_B);
  Multiplexer multiplexer_2 (.in0(A[3]), .in1(B[3]), .out(Minus_Ans[3]), .sel(not_4_out));
  not not_4 (not_4_out, A_GreaterThan_B);
  Multiplexer #(.width(4)) multiplexer_3 (.in0({A[3], A_Plus_B[2:0]}), .in1(Minus_Ans), .out(Result), .sel(not_5_out));
  not not_5 (not_5_out, IsSameSign);

  // Other names for the same wires on the sheet: A_Unsigned[2:0] = A[2:0]; B_Sign = B[3]; B_Unsigned[2:0] = B[2:0];
  //   Plus_Ans[3:0] = {A[3], A_Plus_B[2:0]}; A_Sign = A[3]
endmodule

module TrueForm_Adder_Display (
  input  [3:0] A,
  input  [3:0] B
);

  wire trueform_seperator_1_sign, trueform_seperator_2_sign, trueform_seperator_3_sign;
  wire [3:0] trueform_seperator_1_value, trueform_seperator_2_value, trueform_seperator_3_value,
       tureform_adder_4bit_1_result;

  _7_Segment_Display u_7_segment_display_1 (.g(trueform_seperator_1_sign));  // open: f, a, b, e, d, c, dp
  _7_Segment_Display u_7_segment_display_2 (.g(trueform_seperator_2_sign));  // open: f, a, b, e, d, c, dp
  Hex_Digit_Display hex_digit_display_1 (.value(trueform_seperator_1_value));  // open: dp
  TrueForm_Seperator trueform_seperator_1 (
    .number(A), .value(trueform_seperator_1_value), .sign(trueform_seperator_1_sign));
  Hex_Digit_Display hex_digit_display_2 (.value(trueform_seperator_2_value));  // open: dp
  TrueForm_Seperator trueform_seperator_2 (
    .number(B), .value(trueform_seperator_2_value), .sign(trueform_seperator_2_sign));
  _7_Segment_Display u_7_segment_display_3 (.g(trueform_seperator_3_sign));  // open: f, a, b, e, d, c, dp
  TureForm_Adder_4bit tureform_adder_4bit_1 (.A(A), .B(B), .Result(tureform_adder_4bit_1_result));
  Hex_Digit_Display hex_digit_display_3 (.value(trueform_seperator_3_value));  // open: dp
  TrueForm_Seperator trueform_seperator_3 (
    .number(tureform_adder_4bit_1_result), .value(trueform_seperator_3_value),
    .sign(trueform_seperator_3_sign));
endmodule

module TrueForm_Seperator (
  input  [3:0] number,
  output [3:0] value,
  output sign
);


  assign sign = number[3];
  assign value = {1'b0, number[2:0]};
endmodule

module Twos_Complement_Adder_4bit (
  input  [3:0] A,
  input  [3:0] B,
  input  carry_in,
  output carry_out,
  output [3:0] sum,
  output overflow
);

  wire not_1_out, xor_1_out, xor_2_out;

  adder_4bit adder_4bit_1 (.A(A), .B(B), .carry_in(carry_in), .carry_out(carry_out), .sum(sum));
  xor xor_1 (xor_1_out, A[3], B[3]);
  not not_1 (not_1_out, xor_1_out);
  xor xor_2 (xor_2_out, B[3], sum[3]);
  and and_1 (overflow, not_1_out, xor_2_out);

  // Other names for the same wires on the sheet: A_Sign = A[3]; B_Sign = B[3]; Sum_Sign = sum[3]
endmodule
