// Logisim project Subtracter.circ as structural Verilog: 4 circuits, main circuit main
module main (
  input  [3:0] A,
  input  [3:0] B
);

  wire borrow_p1, subtracter_4bit_1_borrow_out;
  wire [3:0] subtracter_4bit_1_diff;

  Hex_Digit_Display hex_digit_display_1 (.value(A));  // open: dp
  Hex_Digit_Display hex_digit_display_2 (.value(B));  // open: dp
  // DipSwitch #(.number(1)) borrow: pin names not known; wires that end beside it: borrow_p1
  Hex_Digit_Display hex_digit_display_3 (.value(subtracter_4bit_1_diff));  // open: dp
  Subtracter_4bit subtracter_4bit_1 (
    .borrow_in(borrow_p1), .A(A), .B(B), .diff(subtracter_4bit_1_diff),
    .borrow_out(subtracter_4bit_1_borrow_out));
  LED led_1 (.in(subtracter_4bit_1_borrow_out));
endmodule

module Full_Subtracter (
  input  bit_1,
  input  bit_0,
  input  borrow_in,
  output borrow_out,
  output diff
);

  wire half_subtracter_1_borrow, half_subtracter_1_diff, half_subtracter_2_borrow;

  Half_Subtracter half_subtracter_1 (
    .bit_1(bit_1), .bit_0(bit_0), .borrow(half_subtracter_1_borrow), .diff(half_subtracter_1_diff));
  Half_Subtracter half_subtracter_2 (
    .bit_1(half_subtracter_1_diff), .bit_0(borrow_in), .borrow(half_subtracter_2_borrow), .diff(diff));
  or or_1 (borrow_out, half_subtracter_1_borrow, half_subtracter_2_borrow);
endmodule

module Half_Subtracter (
  input  bit_1,
  input  bit_0,
  output borrow,
  output diff
);

  wire not_1_out;

  not not_1 (not_1_out, bit_1);
  and and_1 (borrow, not_1_out, bit_0);
  xor xor_1 (diff, bit_1, bit_0);
endmodule

module Subtracter_4bit (
  input  borrow_in,
  input  [3:0] A,
  input  [3:0] B,
  output [3:0] diff,
  output borrow_out
);

  wire full_subtracter_1_borrow_out, full_subtracter_2_borrow_out, full_subtracter_3_borrow_out;

  Full_Subtracter full_subtracter_1 (
    .bit_1(A[0]), .bit_0(B[0]), .borrow_in(borrow_in), .borrow_out(full_subtracter_1_borrow_out),
    .diff(diff[0]));
  Full_Subtracter full_subtracter_2 (
    .bit_1(A[1]), .bit_0(B[1]), .borrow_in(full_subtracter_1_borrow_out),
    .borrow_out(full_subtracter_2_borrow_out), .diff(diff[1]));
  Full_Subtracter full_subtracter_3 (
    .bit_1(A[2]), .bit_0(B[2]), .borrow_in(full_subtracter_2_borrow_out),
    .borrow_out(full_subtracter_3_borrow_out), .diff(diff[2]));
  Full_Subtracter full_subtracter_4 (
    .bit_1(A[3]), .bit_0(B[3]), .borrow_in(full_subtracter_3_borrow_out), .borrow_out(borrow_out),
    .diff(diff[3]));

  // Other names for the same wires on the sheet: A_0 = A[0]; A_1 = A[1]; A_2 = A[2]; A_3 = A[3]; B_0 = B[0];
  //   B_1 = B[1]; B_2 = B[2]; B_3 = B[3]
endmodule
