// Logisim project Signal.circ as structural Verilog: 8 circuits, main circuit main
module main (
);

  wire clock_1_out, d_flip_flop_1_not_q, d_flip_flop_1_q, dipswitch_1_sw1;

  Clock clock_1 (.out(clock_1_out));
  DipSwitch #(.number(1)) dipswitch_1 (.sw1(dipswitch_1_sw1));
  D_Flip_Flop d_flip_flop_1 (
    .D(d_flip_flop_1_not_q), .clock(clock_1_out), .enable(dipswitch_1_sw1), .Q(d_flip_flop_1_q),
    .Not_Q(d_flip_flop_1_not_q));  // open: reset
  LED led_1 (.in(d_flip_flop_1_q));
endmodule

module SR_Latch (
  input  R,
  input  S,
  output Q,
  output Not_Q
);

  nor nor_1 (Q, R, Not_Q);
  nor nor_2 (Not_Q, Q, S);
endmodule

module D_Latch (
  input  D,
  input  WE,
  input  reset,
  output Q,
  output Not_Q
);

  wire and_1_out, and_2_out, and_3_out, not_1_out, not_2_out, or_1_out;

  not not_1 (not_1_out, D);
  and and_1 (and_1_out, not_1_out, WE);
  and and_2 (and_2_out, WE, D);
  or or_1 (or_1_out, and_1_out, reset);
  not not_2 (not_2_out, reset);
  and and_3 (and_3_out, not_2_out, and_2_out);
  SR_Latch sr_latch_1 (.R(or_1_out), .S(and_3_out), .Q(Q), .Not_Q(Not_Q));
endmodule

module D_Flip_Flop (
  input  D,
  input  clock,
  input  enable,
  input  reset,
  output Q,
  output Not_Q
);

  wire and_1_out, d_latch_1_q, not_1_out;

  not not_1 (not_1_out, clock);
  D_Latch d_latch_1 (.D(D), .WE(not_1_out), .reset(reset), .Q(d_latch_1_q));  // open: Not_Q
  and and_1 (and_1_out, enable, clock);
  D_Latch d_latch_2 (.D(d_latch_1_q), .WE(and_1_out), .reset(reset), .Q(Q), .Not_Q(Not_Q));
endmodule

module D_Flip_Flop_Falling (
  input  D,
  input  clock,
  input  reset,
  output Q,
  output Not_Q
);

  wire d_latch_1_q, not_1_out;

  D_Latch d_latch_1 (.D(D), .WE(clock), .reset(reset), .Q(d_latch_1_q));  // open: Not_Q
  not not_1 (not_1_out, clock);
  D_Latch d_latch_2 (.D(d_latch_1_q), .WE(not_1_out), .reset(reset), .Q(Q), .Not_Q(Not_Q));
endmodule

module Register_4bit (
  input  [3:0] D,
  input  enable,
  input  clock,
  input  reset,
  output [3:0] Q
);

  D_Flip_Flop d_flip_flop_1 (.D(D[0]), .clock(clock), .enable(enable), .reset(reset), .Q(Q[0]));  // open: Not_Q
  D_Flip_Flop d_flip_flop_2 (.D(D[1]), .clock(clock), .enable(enable), .reset(reset), .Q(Q[1]));  // open: Not_Q
  D_Flip_Flop d_flip_flop_3 (.D(D[2]), .clock(clock), .enable(enable), .reset(reset), .Q(Q[2]));  // open: Not_Q
  D_Flip_Flop d_flip_flop_4 (.D(D[3]), .clock(clock), .enable(enable), .reset(reset), .Q(Q[3]));  // open: Not_Q
endmodule

module Counter_4bit (
  input  enable,
  input  clock,
  input  reset,
  output [3:0] value
);

  wire [3:0] adder_1_out;

  Register_4bit register_4bit_1 (.D(adder_1_out), .enable(enable), .clock(clock), .reset(reset), .Q(value));
  Adder #(.width(4)) adder_1 (.a(4'b0001), .b(value), .out(adder_1_out));  // open: cin, cout
endmodule

module Array_Sum (
);

  wire button_1_out, clock_1_out;
  wire [7:0] adder_1_out, counter_1_q, register_1_q;

  Button button_1 (.out(button_1_out));
  Clock clock_1 (.out(clock_1_out));
  Counter counter_1 (.clr(button_1_out), .load(1'b0), .clk(clock_1_out), .Q(counter_1_q));  // open: up, count, D, carry
  Register register_1 (.D(adder_1_out), .en(clock_1_out), .clk(clock_1_out), .Q(register_1_q), .clr(button_1_out));
  Adder adder_1 (.a(counter_1_q), .b(register_1_q), .out(adder_1_out));  // open: cin, cout
endmodule
