// Logisim project Decoders.circ as structural Verilog: 3 circuits, main circuit Decoder2To4
module Decoder2To4 (
  input  A1,
  input  A0,
  output Y0,
  output Y1,
  output Y2,
  output Y3
);

  wire not_1_out, not_2_out;

  not not_1 (not_1_out, A1);
  not not_2 (not_2_out, A0);
  and and_1 (Y0, not_1_out, not_2_out);
  and and_2 (Y1, not_1_out, A0);
  and and_3 (Y2, A1, not_2_out);
  and and_4 (Y3, A1, A0);
endmodule

module Decoder3To8 (
  input  A2,
  input  A1,
  input  A0,
  output Y0,
  output Y1,
  output Y2,
  output Y3,
  output Y4,
  output Y5,
  output Y6,
  output Y7
);

  wire not_1_out, not_2_out, not_3_out;

  not not_1 (not_1_out, A2);
  not not_2 (not_2_out, A1);
  not not_3 (not_3_out, A0);
  and and_1 (Y0, not_3_out, not_2_out, not_1_out);
  and and_2 (Y1, not_1_out, not_2_out, A0);
  and and_3 (Y2, not_3_out, A1, not_1_out);
  and and_4 (Y3, not_1_out, A1, A0);
  and and_5 (Y4, A2, not_2_out, not_3_out);
  and and_6 (Y5, A0, not_2_out, A2);
  and and_7 (Y6, A2, A1, not_3_out);
  and and_8 (Y7, A0, A1, A2);
endmodule

module Decoder4To16 (
  input  A3,
  input  A2,
  input  A1,
  input  A0,
  output Y0,
  output Y1,
  output Y2,
  output Y3,
  output Y4,
  output Y5,
  output Y6,
  output Y7,
  output Y8,
  output Y9,
  output Y10,
  output Y11,
  output Y12,
  output Y13,
  output Y14,
  output Y15
);

  wire not_1_out, not_2_out, not_3_out, not_4_out;

  not not_1 (not_1_out, A3);
  not not_2 (not_2_out, A2);
  not not_3 (not_3_out, A1);
  not not_4 (not_4_out, A0);
  and and_1 (Y0, not_1_out, not_2_out, not_3_out, not_4_out);
  and and_2 (Y1, not_1_out, not_2_out, not_3_out, A0);
  and and_3 (Y2, not_1_out, not_2_out, A1, not_4_out);
  and and_4 (Y3, not_1_out, not_2_out, A1, A0);
  and and_5 (Y4, not_1_out, A2, not_3_out, not_4_out);
  and and_6 (Y5, not_1_out, A2, not_3_out, A0);
  and and_7 (Y6, not_1_out, A2, A1, not_4_out);
  and and_8 (Y7, not_1_out, A2, A1, A0);
  and and_9 (Y8, A3, not_2_out, not_3_out, not_4_out);
  and and_10 (Y9, A3, not_2_out, not_3_out, A0);
  and and_11 (Y10, A3, not_2_out, A1, not_4_out);
  and and_12 (Y11, A3, not_2_out, A1, A0);
  and and_13 (Y12, A3, A2, not_3_out, not_4_out);
  and and_14 (Y13, A3, A2, not_3_out, A0);
  and and_15 (Y14, A3, A2, A1, not_4_out);
  and and_16 (Y15, A3, A2, A1, A0);
endmodule
