// Logisim project Xor.circ as structural Verilog: 1 circuit, main circuit main
module main (
  input  A,
  input  B,
  output STD_Out,
  output Test_Out
);

  wire nand_1_out, or_1_out;

  xor xor_1 (STD_Out, A, B);
  nand nand_1 (nand_1_out, A, B);
  or or_1 (or_1_out, A, B);
  and and_1 (Test_Out, nand_1_out, or_1_out);
endmodule
