// Logisim project OwnROM.circ as structural Verilog: 3 circuits, main circuit main
module main (
);

  wire clock_1_out, clock_2_out, reset;
  wire [7:0] CMD, PC;

  Clock clock_1 (.out(clock_1_out));
  Counter counter_1 (.clr(reset), .clk(clock_1_out), .Q(PC));  // open: load, up, count, D, carry
  Button button_1 (.out(reset));
  // Probe on PC
  Clock clock_2 (.out(clock_2_out));
  RAM ram_1 (.addr(PC), .oe(1'b1), .clk(clock_2_out), .dout(CMD));  // open: we, din
  // Probe on CMD
endmodule

module Rom16x8 (
  input  [3:0] S,
  output [7:0] Q
);

  wire [7:0] multiplexer_1_out, multiplexer_2_out, multiplexer_3_out, multiplexer_4_out, multiplexer_5_out,
       multiplexer_6_out, multiplexer_7_out, multiplexer_8_out, multiplexer_9_out, multiplexer_10_out,
       multiplexer_11_out, multiplexer_12_out, multiplexer_13_out, multiplexer_14_out, register_1_q,
       register_2_q, register_3_q, register_4_q, register_5_q, register_6_q, register_7_q, register_8_q,
       register_9_q, register_10_q, register_11_q, register_12_q, register_13_q, register_14_q,
       register_15_q, register_16_q;

  Register register_1 (.Q(register_1_q));  // open: D, en, clk, clr
  Register register_2 (.Q(register_2_q));  // open: D, en, clk, clr
  Register register_3 (.Q(register_3_q));  // open: D, en, clk, clr
  Register register_4 (.Q(register_4_q));  // open: D, en, clk, clr
  Register register_5 (.Q(register_5_q));  // open: D, en, clk, clr
  Register register_6 (.Q(register_6_q));  // open: D, en, clk, clr
  Register register_7 (.Q(register_7_q));  // open: D, en, clk, clr
  Register register_8 (.Q(register_8_q));  // open: D, en, clk, clr
  Register register_9 (.Q(register_9_q));  // open: D, en, clk, clr
  Register register_10 (.Q(register_10_q));  // open: D, en, clk, clr
  Register register_11 (.Q(register_11_q));  // open: D, en, clk, clr
  Register register_12 (.Q(register_12_q));  // open: D, en, clk, clr
  Register register_13 (.Q(register_13_q));  // open: D, en, clk, clr
  Register register_14 (.Q(register_14_q));  // open: D, en, clk, clr
  Register register_15 (.Q(register_15_q));  // open: D, en, clk, clr
  Register register_16 (.Q(register_16_q));  // open: D, en, clk, clr
  Multiplexer #(.width(8)) multiplexer_1 (.in0(register_1_q), .in1(register_2_q), .out(multiplexer_1_out), .sel(S[0]));
  Multiplexer #(.width(8)) multiplexer_2 (
    .in0(multiplexer_1_out), .in1(multiplexer_3_out), .out(multiplexer_2_out), .sel(S[1]));
  Multiplexer #(.width(8)) multiplexer_3 (.in0(register_3_q), .in1(register_4_q), .out(multiplexer_3_out), .sel(S[0]));
  Multiplexer #(.width(8)) multiplexer_4 (.in0(register_5_q), .in1(register_6_q), .out(multiplexer_4_out), .sel(S[0]));
  Multiplexer #(.width(8)) multiplexer_5 (
    .in0(multiplexer_4_out), .in1(multiplexer_6_out), .out(multiplexer_5_out), .sel(S[1]));
  Multiplexer #(.width(8)) multiplexer_6 (.in0(register_7_q), .in1(register_8_q), .out(multiplexer_6_out), .sel(S[0]));
  Multiplexer #(.width(8)) multiplexer_7 (.in0(register_9_q), .in1(register_10_q), .out(multiplexer_7_out), .sel(S[0]));
  Multiplexer #(.width(8)) multiplexer_8 (
    .in0(multiplexer_7_out), .in1(multiplexer_9_out), .out(multiplexer_8_out), .sel(S[1]));
  Multiplexer #(.width(8)) multiplexer_9 (
    .in0(register_11_q), .in1(register_12_q), .out(multiplexer_9_out), .sel(S[0]));
  Multiplexer #(.width(8)) multiplexer_10 (
    .in0(register_13_q), .in1(register_14_q), .out(multiplexer_10_out), .sel(S[0]));
  Multiplexer #(.width(8)) multiplexer_11 (
    .in0(multiplexer_10_out), .in1(multiplexer_12_out), .out(multiplexer_11_out), .sel(S[1]));
  Multiplexer #(.width(8)) multiplexer_12 (
    .in0(register_15_q), .in1(register_16_q), .out(multiplexer_12_out), .sel(S[0]));
  Multiplexer #(.width(8)) multiplexer_13 (
    .in0(multiplexer_2_out), .in1(multiplexer_5_out), .out(multiplexer_13_out), .sel(S[2]));
  Multiplexer #(.width(8)) multiplexer_14 (
    .in0(multiplexer_8_out), .in1(multiplexer_11_out), .out(multiplexer_14_out), .sel(S[2]));
  Multiplexer #(.width(8)) multiplexer_15 (.in0(multiplexer_13_out), .in1(multiplexer_14_out), .out(Q), .sel(S[3]));

  // Other names for the same wires on the sheet: S_0 = S[0]; S_1 = S[1]; S_2 = S[2]; S_3 = S[3]
endmodule

module RAM2x8 (
  input  [7:0] D,
  input  addr_0,
  input  addr_1,
  input  reset,
  input  enable,
  input  clock,
  output [7:0] Q
);

  wire and_1_out, and_2_out, and_3_out, and_4_out, not_1_out, not_2_out, not_3_out, not_4_out;
  wire [7:0] multiplexer_1_out, multiplexer_2_out, register_1_q, register_2_q, register_3_q, register_4_q;

  not not_1 (not_1_out, addr_0);
  not not_2 (not_2_out, addr_1);
  not not_3 (not_3_out, addr_1);
  not not_4 (not_4_out, addr_0);
  and and_1 (and_1_out, not_1_out, not_2_out, enable);
  and and_2 (and_2_out, addr_0, not_3_out, enable);
  and and_3 (and_3_out, not_4_out, addr_1, enable);
  and and_4 (and_4_out, addr_0, addr_1, enable);
  Register register_1 (.D(D), .en(and_1_out), .clk(clock), .Q(register_1_q), .clr(reset));
  Register register_2 (.D(D), .en(and_2_out), .clk(clock), .Q(register_2_q), .clr(reset));
  Register register_3 (.D(D), .en(and_3_out), .clk(clock), .Q(register_3_q), .clr(reset));
  Register register_4 (.D(D), .en(and_4_out), .clk(clock), .Q(register_4_q), .clr(reset));
  // Probe on register_1_q
  // Probe on register_3_q
  // Probe on register_2_q
  Multiplexer #(.width(8)) multiplexer_1 (
    .in0(register_1_q), .in1(register_2_q), .out(multiplexer_1_out), .sel(addr_0));
  Multiplexer #(.width(8)) multiplexer_2 (
    .in0(register_3_q), .in1(register_4_q), .out(multiplexer_2_out), .sel(addr_0));
  // Probe on register_4_q
  Multiplexer #(.width(8)) multiplexer_3 (.in0(multiplexer_1_out), .in1(multiplexer_2_out), .out(Q), .sel(addr_1));
  // Probe on multiplexer_1_out
  // Probe on multiplexer_2_out

  // Other names for the same wires on the sheet: S_0 = addr_0; S_1 = addr_1
endmodule
